# Fritzing sketch ds3221 connection (saved by Fritzing 0.9.3b)
circuit board: 13.3294cm x 7.90547cm
breadboards: 1

parts:
  Часть1 = Arduino Mega ADK (Rev3)
  Часть2 = Adafruit DS3231 [part_number="Adafruit #3013"]

nets:
  N1: Часть1.D21/SCL, Часть2.SCL
  N2: Часть1.D20/SDA, Часть2.SDA
  5V: Часть1.5V, Часть1.IOREF, Часть2.Vin
  GND: Часть1.GND, Часть2.GND

custom parts:
  Adafruit DS3231: The datasheet for the DS3231 explains that this part is an "Extremely Accurate I²C-Integrated RTC/TCXO/Crystal". And, hey, it does exactly what it says on the tin! This Real Time Clock (RTC) is the most precise you can get in a small, low power package. Most RTCs use an external 32kHz timing crystal that is used to keep time with low current draw. And that's all well and good, but those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
